# Fritzing sketch FamilyForecast (saved by Fritzing 0.9.4)
breadboards: 1

parts:
  part = 8x8 LED Modul mit MAX7219 [package=THT]
  part_2 = Arduino Mega 2560 (Rev3)
  part_3 = IR Receiver Breakout [package=PCB]
  part_4 = Basic Servo
  part_5 = Trimmer Potentiometer [maximum_resistance=10kΩ package=THT]
  part_6 = LCD screen
  part_7 = Resistor [tolerance=±5% resistance=220 package="0805 [SMD]"]

nets (from the schematic view):
  VCC: part.VCC_Eingang, part_2.5V, part_3.VCC, part_4.vcc, part_5.leg1, part_6.VDD, part_7.Pin_1
  GND: part.GND_Eingang, part_2.GND, part_3.GND, part_4.gnd, part_5.wiper, part_6.VSS, part_6.R/W, part_6.LED-
  N1: part.DIN_Eingang, part_2.D12_PWM
  N2: part.CS_Eingang, part_2.D10_PWM
  N3: part.CLK_Eingang, part_2.D11_PWM
  N4: part_2.D26, part_4.pulse
  N5: part_2.D32, part_6.DB5
  N6: part_2.D33, part_6.DB4
  N7: part_2.D34, part_6.DB7
  N8: part_2.D35, part_6.DB6
  N9: part_2.D50, part_6.RS
  N10: part_2.D51, part_6.E
  N11: part_2.D53, part_3.OUT
  N12: part_5.leg2, part_6.V0
  N13: part_6.LED+, part_7.Pin_0
