# Fritzing sketch Hello_World (saved by Fritzing 0.9.4)
breadboards: 2

parts:
  Part1 = Arduino Mega 2560 (Rev3)
  LCD1 = LCD screen
  S1 = Pushbutton [package="[THT]"]
  R2 = Trimmer Potentiometer [maximum_resistance=10kΩ package=THT]
  R3 = Resistor [tolerance=±5% resistance=10k package=THT]
  R4 = Resistor [tolerance=±5% resistance=220 package=THT]
  LED1 = LED - 5mm [color="Red (633nm)" package="5 mm [THT]"]
  LED2 = LED - 5mm [color="Red (633nm)" package="5 mm [THT]"]
  LED3 = LED - 5mm [color="Blue (470nm)" package="5 mm [THT]"]
  LED4 = LED - 5mm [color="Red (633nm)" package="5 mm [THT]"]
  LED5 = LED - 5mm [color="Red (633nm)" package="5 mm [THT]"]
  R5 = Resistor [tolerance=±5% resistance=220 package=THT]
  R6 = Resistor [tolerance=±5% resistance=220 package=THT]
  R7 = Resistor [tolerance=±5% resistance=220 package=THT]
  R8 = Resistor [tolerance=±5% resistance=220 package=THT]
  R9 = Resistor [tolerance=±5% resistance=220 package=THT]
  HC-SR04_Sensor_1 = HC-SR04 Ultrasonic Distance Sensor

nets (from the schematic view):
  N1: Part1.D11_PWM, HC-SR04_Sensor_1.GND
  N2: Part1.D10_PWM, HC-SR04_Sensor_1.TRIG
  N3: Part1.IOREF, LCD1.VDD
  5V: Part1.5V, S1.Pin_3, S1.Pin_4, R2.leg1, R3.Pin_0, R4.Pin_0, HC-SR04_Sensor_1.VCC
  GND: Part1.GND, LCD1.VSS, LCD1.R/W, LCD1.LED-, R2.wiper, R3.Pin_1, R5.Pin_1, R6.Pin_1, R7.Pin_1, R8.Pin_1, R9.Pin_1, HC-SR04_Sensor_1.ECHO
  N4: Part1.D2_PWM, LED5.anode
  N5: Part1.D3_PWM, LED4.anode
  N6: Part1.D4_PWM, LED3.anode
  N7: Part1.D5_PWM, LED2.anode
  N8: Part1.D6_PWM, LED1.anode
  N9: Part1.D7_PWM, S1.Pin_1, S1.Pin_2
  N10: Part1.D22, LCD1.RS
  N11: Part1.D23, LCD1.E
  N12: Part1.D32, LCD1.DB7
  N13: Part1.D33, LCD1.DB6
  N14: Part1.D34, LCD1.DB5
  N15: Part1.D35, LCD1.DB4
  N16: LCD1.V0, R2.leg2
  N17: LCD1.LED+, R4.Pin_1
  N18: LED1.cathode, R5.Pin_0
  N19: LED2.cathode, R6.Pin_0
  N20: LED3.cathode, R7.Pin_0
  N21: LED4.cathode, R8.Pin_0
  N22: LED5.cathode, R9.Pin_0
