# Fritzing sketch RGB_Roman (saved by Fritzing 0.9.4)
breadboards: 1

parts:
  LED2 = RGB LED (com. cathode, rbg) [package="5 mm [THT]"]
  R1 = Resistor [tolerance=±5% resistance=330 package=THT]
  R2 = Resistor [tolerance=±5% resistance=330 package=THT]
  R3 = Resistor [tolerance=±5% resistance=330 package=THT]
  part = Arduino Mega 2560 (Rev3)
  part_2 = IR Receiver Breakout [package=PCB]
  LED5 = RGB LED (com. cathode, rbg) [package="5 mm [THT]"]
  LED4 = RGB LED (com. cathode, rbg) [package="5 mm [THT]"]
  LED3 = RGB LED (com. cathode, rbg) [package="5 mm [THT]"]
  LED9 = RGB LED (com. cathode, rbg) [package="5 mm [THT]"]
  LED1 = RGB LED (com. cathode, rbg) [package="5 mm [THT]"]
  LED7 = RGB LED (com. cathode, rbg) [package="5 mm [THT]"]
  LED8 = RGB LED (com. cathode, rbg) [package="5 mm [THT]"]
  LED6 = RGB LED (com. cathode, rbg) [package="5 mm [THT]"]

nets (from the schematic view):
  N1: LED2.red_anode, R3.Pin_1, LED5.red_anode, LED4.red_anode, LED3.red_anode, LED9.red_anode, LED1.red_anode, LED7.red_anode, LED8.red_anode, LED6.red_anode
  GND: LED2.common_cathode, part.GND, part_2.GND, LED5.common_cathode, LED4.common_cathode, LED3.common_cathode, LED9.common_cathode, LED1.common_cathode, LED7.common_cathode, LED8.common_cathode, LED6.common_cathode
  N2: LED2.blue_anode, R2.Pin_1, LED5.blue_anode, LED4.blue_anode, LED3.blue_anode, LED9.blue_anode, LED1.blue_anode, LED7.blue_anode, LED8.blue_anode, LED6.blue_anode
  N3: LED2.green_anode, R1.Pin_1, LED5.green_anode, LED4.green_anode, LED3.green_anode, LED9.green_anode, LED1.green_anode, LED7.green_anode, LED8.green_anode, LED6.green_anode
  N4: R1.Pin_0, part.D5_PWM
  N5: R2.Pin_0, part.D6_PWM
  N6: R3.Pin_0, part.D4_PWM
  5V: part.5V, part_2.VCC
  N7: part.D3_PWM, part_2.OUT
