# Fritzing sketch dance-dance-interactions (saved by Fritzing 0.9.4)
breadboards: 1

parts:
  part = Piezo Speaker
  part_2 = HC-SR04 Ultrasonic Distance Sensor
  part_3 = HC-SR04 Ultrasonic Distance Sensor
  part_4 = HC-SR04 Ultrasonic Distance Sensor
  part_5 = Arduino Mega 2560 (Rev3)

nets (from the schematic view):
  N1: part.pin1, part_5.D10_PWM
  N2: part.pin2, part_2.ECHO, part_3.ECHO, part_4.ECHO, part_5.GND
  VCC: part_2.VCC, part_3.VCC, part_4.VCC, part_5.5V
  N3: part_2.TRIG, part_5.D8_PWM
  N4: part_2.GND, part_5.D9_PWM
  N5: part_3.TRIG, part_5.D7_PWM
  N6: part_3.GND, part_5.D6_PWM
  N7: part_4.TRIG, part_5.D4_PWM
  N8: part_4.GND, part_5.D5_PWM
